# Fritzing sketch Sleep_coach_schematic (saved by Fritzing 0.7.12b)
breadboards: 1

parts:
  XTAL2 = Crystal [frequency="16 Mhz" package=THT]
  C6 = Ceramic Capacitor [capacitance=100nF package="100 mil [THT, multilayer]"]
  C7 = Ceramic Capacitor [capacitance=100nF package="100 mil [THT, multilayer]"]
  U4 = Voltage Regulator - 5V [package="TO220 [THT]"]
  C8 = Electrolytic Capacitor [capacitance=10µF package="100 mil [THT, electrolytic]"]
  C9 = Electrolytic Capacitor [capacitance=10µF package="100 mil [THT, electrolytic]"]
  Power_plug2 = Power plug
  U3 = atmega328 [package=dip]
  LED1 = LED - 5mm [color="Blue (525nm)" package="5 mm [THT]"]
  LED2 = LED - 5mm [color="Blue (525nm)" package="5 mm [THT]"]
  LED3 = LED - 5mm [color="Blue (525nm)" package="5 mm [THT]"]
  LED4 = LED - 5mm [color="Blue (525nm)" package="5 mm [THT]"]
  S1 = Pushbutton [package="[THT]"]
  R1 = Resistor [tolerance=±5% resistance=220 package=THT]

nets:
  N1: XTAL2.pin_0, C7.1, U3.XLAT1
  N2: XTAL2.pin_1, C6.1, U3.XLAT2
  GND: C6.0, C7.0, U4.GND, C8.-, C9.-, Power_plug2.GND, U3.GND, LED1.cathode, LED2.cathode, LED3.cathode, LED4.cathode, R1.Pin_0
  N3: U4.input_voltage, C9.+, Power_plug2.VCC
  N4: U4.output_voltage, C8.+, U3.VCC, U3.AVCC, U3.AREF, S1.Pin_1, S1.Pin_2
  N5: U3.D5_(PWM), LED1.anode
  N6: U3.D6_(PWM), LED2.anode
  N7: U3.D9_(PWM), LED4.anode
  N8: U3.D10_(PWM), LED3.anode
  N9: U3.D11_(PWM), S1.Pin_3, S1.Pin_4, R1.Pin_1
